# Fritzing sketch schematic (saved by Fritzing 0.9.5d)
breadboards: 1

parts:
  Teensy_3_1 = Teensy 3.1
  S1 = SWITCH-MOMENTARY-2 [package=reed_switch_pth]
  U1 = Voltage Regulator - 5V [package="TO220 [THT]"]
  BAT1 = Battery Holders [package=battery-aa]
  S2 = Momentary Switch [package=ksa_sealed_tac_switch]
  LED2 = RGB LED (com. cathode, rgb) [package="5 mm [THT]"]
  LED3 = RGB LED (com. cathode, rgb) [package="5 mm [THT]"]
  LED4 = RGB LED (com. cathode, rgb) [package="5 mm [THT]"]
  R1 = Resistor [tolerance=±5% resistance=220 package=THT]
  R2 = Resistor [tolerance=±5% resistance=220 package=THT]
  R3 = Resistor [tolerance=±5% resistance=220 package=THT]
  R4 = Resistor [tolerance=±5% resistance=220 package=THT]
  R5 = Resistor [tolerance=±5% resistance=220 package=THT]
  R6 = Resistor [tolerance=±5% resistance=220 package=THT]
  R7 = Resistor [tolerance=±5% resistance=220 package=THT]
  R8 = Resistor [tolerance=±5% resistance=220 package=THT]
  R9 = Resistor [tolerance=±5% resistance=220 package=THT]
  SP1 = SPEAKER [package=pcb_mount_speaker]
  M1 = PAM8403 Stereo Amplifier [part_number=HW-104]
  TP1 = TP4056 [chip_label=TP4056 package="DIP (Dual Inline) [THT]"]

nets:
  N1: Teensy_3_1.GND, LED2.common_cathode, LED3.common_cathode, LED4.common_cathode
  N2: Teensy_3_1.D1, R5.Pin_0, R7.Pin_0, R9.Pin_0
  N3: Teensy_3_1.D2, R4.Pin_0, R6.Pin_0, R8.Pin_0
  N4: Teensy_3_1.D3, R1.Pin_0, R2.Pin_0, R3.Pin_0
  N5: Teensy_3_1.D4, M1.INPUTR
  N6: Teensy_3_1.A8/D22, S2.4
  N7: Teensy_3_1.AGND, U1.GND, M1.POWER-, M1.INPUTG, TP1.pin6
  N8: Teensy_3_1.Vin, S1.2, S2.1, M1.POWER+
  N9: S1.1, U1.output_voltage
  N10: U1.input_voltage, TP1.pin3
  N11: BAT1.-, TP1.pin4
  N12: BAT1.+, TP1.pin5
  N13: LED2.red_anode, R3.Pin_1
  N14: LED2.green_anode, R8.Pin_1
  N15: LED2.blue_anode, R9.Pin_1
  N16: LED3.red_anode, R2.Pin_1
  N17: LED3.green_anode, R6.Pin_1
  N18: LED3.blue_anode, R7.Pin_1
  N19: LED4.red_anode, R1.Pin_1
  N20: LED4.green_anode, R4.Pin_1
  N21: LED4.blue_anode, R5.Pin_1
  N22: SP1.+, M1.ROUT+
  N23: SP1.-, M1.ROUT-

custom parts:
  PAM8403 Stereo Amplifier: PAM8403 stereo amplifier module Descriptive words Links: PAM8403 product datasheet
  TP4056: A DIP stand-in part for whatever IC you want. With 6 pins on a 300mil dual inline package (DIP) footprint.
